# Fritzing sketch Garage Sensor PCB Design with Top and Bottom layers (saved by Fritzing 0.9.9b)
circuit board: 11.0152cm x 7.57402cm
breadboards: 1

parts:
  R3L = LED - 5mm [color="Red (633nm)" current=0.030 package="5 mm [THT]"]
  R1L = LED - 5mm [color="Red (633nm)" current=0.030 package="5 mm [THT]"]
  150Ω = Resistor [tolerance=±5% power=0.25 resistance=150 package=THT]
  150Ω_2 = Resistor [tolerance=±5% power=0.25 resistance=150 package=THT]
  150Ω_3 = Resistor [tolerance=±5% power=0.25 resistance=150 package=THT]
  150Ω_4 = Resistor [tolerance=±5% power=0.25 resistance=150 package=THT]
  Y2L = LED - 5mm [color="Yellow (595nm)" current=0.030 package="5 mm [THT]"]
  Y1L = LED - 5mm [color="Yellow (595nm)" current=0.030 package="5 mm [THT]"]
  150Ω_5 = Resistor [tolerance=±5% power=0.25 resistance=150 package=THT]
  G1C = LED - 5mm [color="Green (570nm)" current=0.030 package="5 mm [THT]"]
  150Ω_6 = Resistor [tolerance=±5% power=0.25 resistance=150 package=THT]
  Y1R = LED - 5mm [color="Yellow (595nm)" current=0.030 package="5 mm [THT]"]
  Y2R = LED - 5mm [color="Yellow (595nm)" current=0.030 package="5 mm [THT]"]
  150Ω_7 = Resistor [tolerance=±5% power=0.25 resistance=220 package=THT]
  150Ω_8 = Resistor [tolerance=±5% power=0.25 resistance=150 package=THT]
  R1R = LED - 5mm [color="Red (633nm)" current=0.030 package="5 mm [THT]"]
  R3R = LED - 5mm [color="Red (633nm)" current=0.030 package="5 mm [THT]"]
  150Ω_9 = Resistor [tolerance=±5% power=0.25 resistance=220 package=THT]
  150Ω_10 = Resistor [tolerance=±5% power=0.25 resistance=150 package=THT]
  150Ω_11 = Resistor [tolerance=±5% power=0.25 resistance=220 package=THT]
  R2L = LED - 5mm [color="Red (633nm)" current=0.030 package="5 mm [THT]"]
  R2R = LED - 5mm [color="Red (633nm)" current=0.030 package="5 mm [THT]"]
  Nano = Arduino Nano (Rev3.0)
  HC-SR04_Sensor_1 = HC-SR04 Ultrasonic Distance Sensor
  J1 = female pin header, 2 pins [form="♀ (female)"]
  J2 = female pin header, 2 pins [form="♀ (female)"]

nets:
  N1: R3L.cathode, 150Ω.Pin_1
  N2: R3L.anode, R3R.cathode, R3R.anode, 150Ω_9.Pin_1, Nano.D8
  N3: R1L.cathode, 150Ω_3.Pin_1
  N4: R1L.anode, R1R.cathode, R1R.anode, 150Ω_11.Pin_1, Nano.D6
  GND: 150Ω.Pin_0, 150Ω_2.Pin_0, 150Ω_3.Pin_0, 150Ω_4.Pin_0, 150Ω_5.Pin_0, 150Ω_6.Pin_0, 150Ω_7.Pin_0, 150Ω_8.Pin_0, 150Ω_9.Pin_0, 150Ω_10.Pin_0, 150Ω_11.Pin_0, Nano.GND, HC-SR04_Sensor_1.GND, J2.pin2
  N5: 150Ω_2.Pin_1, R2L.cathode
  N6: 150Ω_4.Pin_1, Y2L.cathode
  N7: Y2L.anode, Y2R.anode, Nano.D5
  N8: Y1L.cathode, 150Ω_5.Pin_1
  N9: Y1L.anode, Y1R.cathode, Y1R.anode, 150Ω_7.Pin_1, Nano.D4
  N10: G1C.cathode, 150Ω_6.Pin_1
  N11: G1C.anode, Nano.D3
  N12: Y2R.cathode, 150Ω_8.Pin_1
  N13: 150Ω_10.Pin_1, R2L.anode, R2R.cathode, R2R.anode, Nano.D7
  N14: Nano.D9, HC-SR04_Sensor_1.TRIG
  N15: Nano.D10, HC-SR04_Sensor_1.ECHO
  5V: Nano.5V, HC-SR04_Sensor_1.VCC, J2.pin1
  N16: Nano.A5, J1.pin1
  N17: Nano.A4, J1.pin2

notes:
  Garage Sensor V1
  Made by: Toph and Jit
  Vcc
  Gnd
  SDA
  SCL
  04/02/22
  LCD
